// Logisim project buildMuxCustom.circ as structural Verilog
module _2_1_MUX (
  input  in_1,
  input  in_2,
  input  in_3,
  output out_4
);

  wire and_1_out, and_2_out, not_1_out;

  not not_1 (not_1_out, in_3);
  and and_1 (and_1_out, in_1, not_1_out);
  or or_1 (out_4, and_1_out, and_2_out);
  and and_2 (and_2_out, in_2, in_3);
endmodule

module _4_1_MUX (
  input  in_00,
  input  in_01,
  input  in_10,
  input  in_11,
  input  sel_0,
  input  sel_1,
  output out
);

  wire n2_1_mux_1_p5, n2_1_mux_2_p4;

  // _2_1_MUX 2_1_mux_1: pin names not known; wires that end beside it: in_00, in_01, in_10, sel_1, n2_1_mux_1_p5
  // _2_1_MUX 2_1_mux_2: pin names not known; wires that end beside it: in_10, in_11, sel_1, n2_1_mux_2_p4
  // _2_1_MUX 2_1_mux_3: pin names not known; wires that end beside it: n2_1_mux_1_p5, n2_1_mux_2_p4, sel_0, out
endmodule
