// Logisim project log.circ as structural Verilog: 1 circuit, main circuit main
module main (
  input  reset,
  output [3:0] count
);

  wire clock_out;
  wire [3:0] adder_1_out, multiplexer_1_out;

  // Probe on adder_1_out
  Multiplexer #(.width(4)) multiplexer_1 (
    .in0(adder_1_out), .in1(4'b0000), .out(multiplexer_1_out), .sel(reset));  // open: en
  Clock clock (.out(clock_out));
  Register #(.width(4)) register_1 (.D(multiplexer_1_out), .Q(count), .clk(clock_out));  // open: en, clr
  Adder #(.width(4)) adder_1 (.a(count), .b(4'b0001), .out(adder_1_out));  // open: cin, cout
endmodule
